# Fritzing sketch CircuitoCuboLED (saved by Fritzing 0.9.3b)
circuit board: 44.4522cm x 7.98035cm
breadboards: 6

parts:
  U1 = 74HC595 [package="DIP16 [THT]"]
  R1 = Resistor [tolerance=±5% resistance=220 package=THT]
  R2 = Resistor [tolerance=±5% resistance=220 package=THT]
  R3 = Resistor [tolerance=±5% resistance=220 package=THT]
  R4 = Resistor [tolerance=±5% resistance=220 package=THT]
  R5 = Resistor [tolerance=±5% resistance=220 package=THT]
  R6 = Resistor [tolerance=±5% resistance=220 package=THT]
  R7 = Resistor [tolerance=±5% resistance=220 package=THT]
  R8 = Resistor [tolerance=±5% resistance=220 package=THT]
  J1 = Screw terminal - 2 pins [package=THT]
  U2 = 74HC595 [package="DIP16 [THT]"]
  R9 = Resistor [tolerance=±5% resistance=220 package=THT]
  R10 = Resistor [tolerance=±5% resistance=220 package=THT]
  R11 = Resistor [tolerance=±5% resistance=220 package=THT]
  R13 = Resistor [tolerance=±5% resistance=220 package=THT]
  R14 = Resistor [tolerance=±5% resistance=220 package=THT]
  R15 = Resistor [tolerance=±5% resistance=220 package=THT]
  R16 = Resistor [tolerance=±5% resistance=220 package=THT]
  JP5 = Header 12 [package=1x12_machine-pin-header_lock.004]
  JP6 = Header 12 [package=1x12_machine-pin-header_lock.004]
  R12 = Resistor [tolerance=±5% resistance=220 package=THT]
  JP7 = FTDI_BASIC [package=ftdi_basic]
  U3 = 74HC595 [package="DIP16 [THT]"]
  R17 = Resistor [tolerance=±5% resistance=220 package=THT]
  R18 = Resistor [tolerance=±5% resistance=220 package=THT]
  JP8 = Header 12 [package=1x12_machine-pin-header_lock.004]
  R19 = Resistor [tolerance=±5% resistance=220 package=THT]
  R20 = Resistor [tolerance=±5% resistance=220 package=THT]
  R21 = Resistor [tolerance=±5% resistance=220 package=THT]
  R22 = Resistor [tolerance=±5% resistance=220 package=THT]
  R23 = Resistor [tolerance=±5% resistance=220 package=THT]
  R24 = Resistor [tolerance=±5% resistance=220 package=THT]
  R25 = Resistor [tolerance=±5% resistance=220 package=THT]
  R26 = Resistor [tolerance=±5% resistance=220 package=THT]
  R27 = Resistor [tolerance=±5% resistance=220 package=THT]
  U4 = 74HC595 [package="DIP16 [THT]"]
  U5 = 74HC595 [package="DIP16 [THT]"]
  R28 = Resistor [tolerance=±5% resistance=220 package=THT]
  JP9 = Header 12 [package=1x12_machine-pin-header_lock.004]
  R29 = Resistor [tolerance=±5% resistance=220 package=THT]
  R30 = Resistor [tolerance=±5% resistance=220 package=THT]
  R31 = Resistor [tolerance=±5% resistance=220 package=THT]
  R32 = Resistor [tolerance=±5% resistance=220 package=THT]
  R33 = Resistor [tolerance=±5% resistance=220 package=THT]
  R34 = Resistor [tolerance=±5% resistance=220 package=THT]
  R35 = Resistor [tolerance=±5% resistance=220 package=THT]
  R36 = Resistor [tolerance=±5% resistance=220 package=THT]
  R37 = Resistor [tolerance=±5% resistance=220 package=THT]
  U6 = 74HC595 [package="DIP16 [THT]"]
  R38 = Resistor [tolerance=±5% resistance=220 package=THT]
  R39 = Resistor [tolerance=±5% resistance=220 package=THT]
  R40 = Resistor [tolerance=±5% resistance=220 package=THT]
  R41 = Resistor [tolerance=±5% resistance=220 package=THT]
  R42 = Resistor [tolerance=±5% resistance=220 package=THT]
  R43 = Resistor [tolerance=±5% resistance=220 package=THT]
  R44 = Resistor [tolerance=±5% resistance=220 package=THT]
  R45 = Resistor [tolerance=±5% resistance=220 package=THT]
  U7 = 74HC595 [package="DIP16 [THT]"]
  R46 = Resistor [tolerance=±5% resistance=220 package=THT]
  R47 = Resistor [tolerance=±5% resistance=220 package=THT]
  R48 = Resistor [tolerance=±5% resistance=220 package=THT]
  R49 = Resistor [tolerance=±5% resistance=220 package=THT]
  R50 = Resistor [tolerance=±5% resistance=220 package=THT]
  R51 = Resistor [tolerance=±5% resistance=220 package=THT]
  R52 = Resistor [tolerance=±5% resistance=220 package=THT]
  R53 = Resistor [tolerance=±5% resistance=220 package=THT]
  R54 = Resistor [tolerance=±5% resistance=220 package=THT]
  JP11 = Header 12 [package=1x12_machine-pin-header_lock.004]
  U8 = 74HC595 [package="DIP16 [THT]"]
  JP12 = Header 12 [package=1x12_machine-pin-header_lock.004]
  R55 = Resistor [tolerance=±5% resistance=220 package=THT]
  R56 = Resistor [tolerance=±5% resistance=220 package=THT]
  R57 = Resistor [tolerance=±5% resistance=220 package=THT]
  R58 = Resistor [tolerance=±5% resistance=220 package=THT]
  R59 = Resistor [tolerance=±5% resistance=220 package=THT]
  R60 = Resistor [tolerance=±5% resistance=220 package=THT]
  R61 = Resistor [tolerance=±5% resistance=220 package=THT]
  R62 = Resistor [tolerance=±5% resistance=220 package=THT]
  U9 = 74HC595 [package="DIP16 [THT]"]
  R63 = Resistor [tolerance=±5% resistance=220 package=THT]
  R64 = Resistor [tolerance=±5% resistance=220 package=THT]
  JP13 = Header 12 [package=1x12_machine-pin-header_lock.004]
  R65 = Resistor [tolerance=±5% resistance=220 package=THT]
  R66 = Resistor [tolerance=±5% resistance=220 package=THT]
  R67 = Resistor [tolerance=±5% resistance=220 package=THT]
  R68 = Resistor [tolerance=±5% resistance=220 package=THT]
  R69 = Resistor [tolerance=±5% resistance=220 package=THT]
  R70 = Resistor [tolerance=±5% resistance=220 package=THT]
  R71 = Resistor [tolerance=±5% resistance=220 package=THT]
  R72 = Resistor [tolerance=±5% resistance=220 package=THT]
  U10 = 74HC595 [package="DIP16 [THT]"]
  U11 = 74HC595 [package="DIP16 [THT]"]
  R73 = Resistor [tolerance=±5% resistance=220 package=THT]
  R74 = Resistor [tolerance=±5% resistance=220 package=THT]
  R75 = Resistor [tolerance=±5% resistance=220 package=THT]
  R76 = Resistor [tolerance=±5% resistance=220 package=THT]
  R77 = Resistor [tolerance=±5% resistance=220 package=THT]
  R78 = Resistor [tolerance=±5% resistance=220 package=THT]
  R79 = Resistor [tolerance=±5% resistance=220 package=THT]
  R80 = Resistor [tolerance=±5% resistance=220 package=THT]
  R81 = Resistor [tolerance=±5% resistance=220 package=THT]
  JP14 = Header 12 [package=1x12_machine-pin-header_lock.004]
  U12 = 74HC595 [package="DIP16 [THT]"]
  JP15 = Header 12 [package=1x12_machine-pin-header_lock.004]
  R82 = Resistor [tolerance=±5% resistance=1k package=THT]
  R83 = Resistor [tolerance=±5% resistance=1k package=THT]
  R84 = Resistor [tolerance=±5% resistance=1k package=THT]
  R85 = Resistor [tolerance=±5% resistance=1k package=THT]
  R86 = Resistor [tolerance=±5% resistance=1k package=THT]
  R87 = Resistor [tolerance=±5% resistance=1k package=THT]
  R89 = Resistor [tolerance=±5% resistance=1k package=THT]
  R90 = Resistor [tolerance=±5% resistance=1k package=THT]
  R91 = Resistor [tolerance=±5% resistance=1k package=THT]
  Q1 = NPN-Transistor [package="TO92 [THT]"]
  Q2 = NPN-Transistor [package="TO92 [THT]"]
  R92 = Resistor [tolerance=±5% resistance=1k package=THT]
  Q3 = NPN-Transistor [package="TO92 [THT]"]
  Q4 = NPN-Transistor [package="TO92 [THT]"]
  R94 = Resistor [tolerance=±5% resistance=1k package=THT]
  Q5 = NPN-Transistor [package="TO92 [THT]"]
  Q6 = NPN-Transistor [package="TO92 [THT]"]
  R95 = Resistor [tolerance=±5% resistance=1k package=THT]
  Q7 = NPN-Transistor [package="TO92 [THT]"]
  Q8 = NPN-Transistor [package="TO92 [THT]"]
  R96 = Resistor [tolerance=±5% resistance=1k package=THT]
  Q9 = NPN-Transistor [package="TO92 [THT]"]
  Q10 = NPN-Transistor [package="TO92 [THT]"]
  R97 = Resistor [tolerance=±5% resistance=1k package=THT]
  Q11 = NPN-Transistor [package="TO92 [THT]"]
  Q12 = NPN-Transistor [package="TO92 [THT]"]
  R98 = Resistor [tolerance=±5% resistance=1k package=THT]
  Q13 = NPN-Transistor [package="TO92 [THT]"]
  R99 = Resistor [tolerance=±5% resistance=1k package=THT]
  Q15 = NPN-Transistor [package="TO92 [THT]"]
  Q16 = NPN-Transistor [package="TO92 [THT]"]
  R100 = Resistor [tolerance=±5% resistance=1k package=THT]
  Q17 = NPN-Transistor [package="TO92 [THT]"]
  Q18 = NPN-Transistor [package="TO92 [THT]"]
  R101 = Resistor [tolerance=±5% resistance=1k package=THT]
  Q14 = NPN-Transistor [package="TO92 [THT]"]
  JP10 = Header 12 [package=1x12_machine-pin-header_lock.004]

nets:
  N1: U1.Q1, R2.Pin_1
  N2: U1.Q2, R3.Pin_1
  N3: U1.Q3, R4.Pin_1
  N4: U1.Q4, R5.Pin_1
  N5: U1.Q5, R6.Pin_1
  N6: U1.Q6, R7.Pin_1
  N7: U1.Q7, R8.Pin_1
  GND: U1.GND, U1.OE, J1.pin1, U2.GND, U2.OE, U3.GND, U3.OE, U4.GND, U4.OE, U5.GND, U5.OE, U6.GND, U6.OE, U7.GND, U7.OE, U8.GND, U8.OE, U9.GND, U9.OE, U10.GND, U10.OE, U11.GND, U11.OE, U12.GND, U12.OE, Q1.E, Q2.E, Q3.E, Q4.E, Q5.E, Q6.E, Q7.E, Q8.E, Q9.E, Q10.E, Q11.E, Q12.E, Q13.E, Q15.E, Q16.E, Q17.E, Q18.E, Q14.E
  N8: U1.Q7', U2.DS
  VCC: U1.MR, U1.VCC, J1.pin2, U2.MR, U2.VCC, U3.MR, U3.VCC, U4.MR, U4.VCC, U5.MR, U5.VCC, U6.MR, U6.VCC, U7.MR, U7.VCC, U8.MR, U8.VCC, U9.MR, U9.VCC, U10.MR, U10.VCC, U11.MR, U11.VCC, U12.MR, U12.VCC, R92.Pin_0, R94.Pin_0, R95.Pin_0, R96.Pin_0, R97.Pin_0, R98.Pin_0, R99.Pin_0, R100.Pin_0, R101.Pin_0
  N9: U1.SH_CP, U2.SH_CP, JP7.4, U3.SH_CP, U4.SH_CP, U5.SH_CP, U6.SH_CP, U7.SH_CP, U8.SH_CP, U9.SH_CP, U10.SH_CP, U11.SH_CP, U12.SH_CP
  N10: U1.ST_CP, U2.ST_CP, JP7.3, U3.ST_CP, U4.ST_CP, U5.ST_CP, U6.ST_CP, U7.ST_CP, U8.ST_CP, U9.ST_CP, U10.ST_CP, U11.ST_CP, U12.ST_CP
  N11: U1.DS, JP7.2
  N12: U1.Q0, R1.Pin_1
  N13: R1.Pin_0, JP5.1
  N14: R2.Pin_0, JP5.2
  N15: R3.Pin_0, JP5.3
  N16: R4.Pin_0, JP5.4
  N17: R5.Pin_0, JP5.5
  N18: R6.Pin_0, JP5.6
  N19: R7.Pin_0, JP5.7
  N20: R8.Pin_0, JP5.8
  N21: U2.Q1, R14.Pin_1
  N22: U2.Q2, R16.Pin_1
  N23: U2.Q3, R9.Pin_1
  N24: U2.Q4, R13.Pin_1
  N25: U2.Q5, R11.Pin_1
  N26: U2.Q6, R10.Pin_1
  N27: U2.Q7, R15.Pin_1
  N28: U2.Q7', U3.DS
  N29: U2.Q0, R12.Pin_1
  N30: R9.Pin_0, JP6.3
  N31: R10.Pin_0, JP6.6
  N32: R11.Pin_0, JP6.5
  N33: R13.Pin_0, JP6.4
  N34: R14.Pin_0, JP6.1
  N35: R15.Pin_0, JP6.7
  N36: R16.Pin_0, JP6.2
  N37: JP5.9, R12.Pin_0
  N38: JP6.8, R17.Pin_0
  N39: JP6.9, R18.Pin_0
  N40: U3.Q1, R18.Pin_1
  N41: U3.Q2, R19.Pin_1
  N42: U3.Q3, R23.Pin_1
  N43: U3.Q4, R26.Pin_1
  N44: U3.Q5, R20.Pin_1
  N45: U3.Q6, R25.Pin_1
  N46: U3.Q7, R27.Pin_1
  N47: U3.Q7', U4.DS
  N48: U3.Q0, R17.Pin_1
  N49: JP8.1, R19.Pin_0
  N50: JP8.2, R23.Pin_0
  N51: JP8.3, R26.Pin_0
  N52: JP8.4, R20.Pin_0
  N53: JP8.5, R25.Pin_0
  N54: JP8.6, R27.Pin_0
  N55: JP8.7, R21.Pin_0
  N56: JP8.8, R22.Pin_0
  N57: JP8.9, R24.Pin_0
  N58: R21.Pin_1, U4.Q0
  N59: R22.Pin_1, U4.Q1
  N60: R24.Pin_1, U4.Q2
  N61: U4.Q3, R28.Pin_1
  N62: U4.Q4, R29.Pin_1
  N63: U4.Q5, R30.Pin_1
  N64: U4.Q6, R31.Pin_1
  N65: U4.Q7, R32.Pin_1
  N66: U4.Q7', U5.DS
  N67: U5.Q1, R34.Pin_1
  N68: U5.Q2, R35.Pin_1
  N69: U5.Q3, R36.Pin_1
  N70: U5.Q4, R37.Pin_1
  N71: U5.Q5, R39.Pin_1
  N72: U5.Q6, R40.Pin_1
  N73: U5.Q7, R41.Pin_1
  N74: U5.Q7', U6.DS
  N75: U5.Q0, R33.Pin_1
  N76: R28.Pin_0, JP9.1
  N77: JP9.2, R29.Pin_0
  N78: JP9.3, R30.Pin_0
  N79: JP9.4, R31.Pin_0
  N80: JP9.5, R32.Pin_0
  N81: JP9.6, R33.Pin_0
  N82: JP9.7, R34.Pin_0
  N83: JP9.8, R35.Pin_0
  N84: JP9.9, R36.Pin_0
  N85: R37.Pin_0, JP10.1
  N86: U6.Q1, R42.Pin_1
  N87: U6.Q2, R43.Pin_1
  N88: U6.Q3, R44.Pin_1
  N89: U6.Q4, R45.Pin_1
  N90: U6.Q5, R46.Pin_1
  N91: U6.Q6, R47.Pin_1
  N92: U6.Q7, R48.Pin_1
  N93: U6.Q7', U7.DS
  N94: U6.Q0, R38.Pin_1
  N95: R38.Pin_0, JP10.5
  N96: R39.Pin_0, JP10.2
  N97: R40.Pin_0, JP10.3
  N98: R41.Pin_0, JP10.4
  N99: R42.Pin_0, JP10.6
  N100: R43.Pin_0, JP10.7
  N101: R44.Pin_0, JP10.8
  N102: R45.Pin_0, JP10.9
  N103: U7.Q1, R50.Pin_1
  N104: U7.Q2, R51.Pin_1
  N105: U7.Q3, R52.Pin_1
  N106: U7.Q4, R53.Pin_1
  N107: U7.Q5, R54.Pin_1
  N108: U7.Q6, R55.Pin_1
  N109: U7.Q7, R56.Pin_1
  N110: U7.Q7', U8.DS
  N111: U7.Q0, R49.Pin_1
  N112: R46.Pin_0, JP11.1
  N113: R47.Pin_0, JP11.2
  N114: R48.Pin_0, JP11.3
  N115: R49.Pin_0, JP11.4
  N116: R50.Pin_0, JP11.5
  N117: R51.Pin_0, JP11.6
  N118: R52.Pin_0, JP11.7
  N119: R53.Pin_0, JP11.8
  N120: R54.Pin_0, JP11.9
  N121: U8.Q1, R58.Pin_1
  N122: U8.Q2, R59.Pin_1
  N123: U8.Q3, R60.Pin_1
  N124: U8.Q4, R61.Pin_1
  N125: U8.Q5, R62.Pin_1
  N126: U8.Q6, R63.Pin_1
  N127: U8.Q7, R64.Pin_1
  N128: U8.Q7', U9.DS
  N129: U8.Q0, R57.Pin_1
  N130: JP12.1, R55.Pin_0
  N131: JP12.2, R56.Pin_0
  N132: JP12.3, R57.Pin_0
  N133: JP12.4, R58.Pin_0
  N134: JP12.5, R59.Pin_0
  N135: JP12.6, R60.Pin_0
  N136: JP12.7, R61.Pin_0
  N137: JP12.8, R62.Pin_0
  N138: JP12.9, R63.Pin_0
  N139: U9.Q1, R66.Pin_1
  N140: U9.Q2, R67.Pin_1
  N141: U9.Q3, R68.Pin_1
  N142: U9.Q4, R69.Pin_1
  N143: U9.Q5, R70.Pin_1
  N144: U9.Q6, R71.Pin_1
  N145: U9.Q7, R72.Pin_1
  N146: U9.Q7', U10.DS
  N147: U9.Q0, R65.Pin_1
  N148: R64.Pin_0, JP13.1
  N149: JP13.2, R65.Pin_0
  N150: JP13.3, R66.Pin_0
  N151: JP13.4, R67.Pin_0
  N152: JP13.5, R68.Pin_0
  N153: JP13.6, R69.Pin_0
  N154: JP13.7, R70.Pin_0
  N155: JP13.8, R71.Pin_0
  N156: JP13.9, R72.Pin_0
  N157: U10.Q1, R74.Pin_1
  N158: U10.Q2, R75.Pin_1
  N159: U10.Q3, R76.Pin_1
  N160: U10.Q4, R77.Pin_1
  N161: U10.Q5, R78.Pin_1
  N162: U10.Q6, R79.Pin_1
  N163: U10.Q7, R80.Pin_1
  N164: U10.Q7', U11.DS
  N165: U10.Q0, R73.Pin_1
  N166: U11.Q1, R82.Pin_1
  N167: U11.Q2, R83.Pin_1
  N168: U11.Q3, R84.Pin_1
  N169: U11.Q4, R85.Pin_1
  N170: U11.Q5, R86.Pin_1
  N171: U11.Q6, R87.Pin_1
  N172: U11.Q7, R90.Pin_1
  N173: U11.Q7', U12.DS
  N174: U11.Q0, R81.Pin_1
  N175: R73.Pin_0, JP14.1
  N176: R74.Pin_0, JP14.2
  N177: R75.Pin_0, JP14.3
  N178: R76.Pin_0, JP14.4
  N179: R77.Pin_0, JP14.5
  N180: R78.Pin_0, JP14.6
  N181: R79.Pin_0, JP14.7
  N182: R80.Pin_0, JP14.8
  N183: R81.Pin_0, JP14.9
  N184: U12.Q1, R91.Pin_1
  N185: U12.Q0, R89.Pin_1
  N186: JP15.1, Q1.C, Q2.C, R92.Pin_1
  N187: JP15.2, Q3.C, Q4.C, R94.Pin_1
  N188: JP15.3, Q5.C, Q6.C, R95.Pin_1
  N189: JP15.4, Q7.C, Q8.C, R96.Pin_1
  N190: JP15.5, Q9.C, Q10.C, R97.Pin_1
  N191: JP15.6, Q11.C, Q12.C, R98.Pin_1
  N192: JP15.7, Q13.C, R99.Pin_1, Q14.C
  N193: JP15.8, Q15.C, Q16.C, R100.Pin_1
  N194: JP15.9, Q17.C, Q18.C, R101.Pin_1
  N195: R82.Pin_0, Q1.B, Q2.B
  N196: R83.Pin_0, Q3.B, Q4.B
  N197: R84.Pin_0, Q5.B, Q6.B
  N198: R85.Pin_0, Q7.B, Q8.B
  N199: R86.Pin_0, Q9.B, Q10.B
  N200: R87.Pin_0, Q11.B, Q12.B
  N201: R89.Pin_0, Q15.B, Q16.B
  N202: R90.Pin_0, Q13.B, Q14.B
  N203: R91.Pin_0, Q17.B, Q18.B

notes:
  Anodos 1
  Anodos 3
  Anodos 2
  Anodos 4
  Anodos 5
  Anodos 7
  Anodos 6
  Anodos 9
  Anodos 8
  Catodos
  Alimentacion 5V
  Datos, Clock y latch
  Alimentación 5V
  ánodos 1
  ánodos 2
  ánodos 3
  ánodos 4
  ánodos 5
  ánodos 6
  ánodos 7
  ánodos 8
  ánodos 9
  Cátodos
